# Fritzing sketch sketch (saved by Fritzing 0.9.3b)
breadboards: 1

parts:
  Raspberry_Pi_1 = Raspberry Pi 3 [part_number=RPI-3-V1.2]
  U1 = POT [package=pot_mammoth]
  U2 = LCD-16X2 [package=lcd-16x2_noholes]
  S1 = Pushbutton [package="[SMD]"]
  Part1 = Arduino Nano (Rev3.0) (ICSP)
  VCC1 = Battery block 9V
  TTP223B1 = TTP223B Capacitive Touch Sensor Module
  R1 = Resistor [tolerance=±5% resistance=1k package="2010 [SMD]"]

nets:
  GND: Raspberry_Pi_1.GND, Raspberry_Pi_1.GIPO18, U1.E, U2.VSS, U2.R_W, U2.DB7, U2.K, Part1.GND, VCC1.-, TTP223B1.GND, R1.Pin_1
  N1: Raspberry_Pi_1.GIPO17, U2.DB6
  N2: Raspberry_Pi_1.GIPO27, S1.Pin_3, S1.Pin_4
  N3: Raspberry_Pi_1.GIPO22, TTP223B1.SIG
  N4: Raspberry_Pi_1.GIPO5, U2.DB4
  N5: Raspberry_Pi_1.GIPO6, U2.DB5
  N6: Raspberry_Pi_1.GIPO21, U2.E
  N7: Raspberry_Pi_1.GIPO12, U2.RS
  N8: Raspberry_Pi_1.GIPO15, Part1.D1/TX
  N9: Raspberry_Pi_1.GIPO14, Part1.D0/RX
  5V: Raspberry_Pi_1.5V, U2.VDD, U2.A, S1.Pin_1, S1.Pin_2, TTP223B1.VCC
  N10: U1.S, Part1.5V
  N11: U1.A, Part1.A0
  N12: U2.VO, R1.Pin_0
  N13: Part1.VIN, VCC1.+

custom parts:
  TTP223B Capacitive Touch Sensor Module: The TTP223B capacitive touch sensor module uses the TTP223B IC. The appropriate voltage is approximately 2 to 5.5 volts.
